# Fritzing sketch 0_10V_input (saved by Fritzing 0.9.0b)
breadboards: 1

parts:
  U2 = LM 358 Dual Op-Amp [package="DIP8 [THT]"]
  R1 = Resistor [tolerance=±5% resistance=10k package=THT]
  R2 = Resistor [tolerance=±5% resistance=10k package=THT]
  U1 = Arduino Uno (Rev3)
  J1 = Screw terminal - 2 pins [package=THT]
  J2 = screw terminal, 3 pins

nets:
  N1: U2.connector0, U2.connector1, R1.Pin_0
  N2: U2.connector2, J1.pin1
  GND: U2.connector3, R2.Pin_1, U1.GND, J1.pin2, J2.pin3
  N3: U2.connector4, R1.Pin_1, R2.Pin_0
  N4: U2.connector5, U2.connector6, U1.A0
  12V: U2.connector7, J2.pin1
  5V: U1.5V, J2.pin2

notes:
  0-10V
  GND
