# Fritzing sketch PWM_to_0_10V (saved by Fritzing 0.8.7b)
breadboards: 1

parts:
  U1 = LM 358 Dual Op-Amp [package="DIP8 [THT]"]
  R1 = Resistor [tolerance=±5% resistance=10k package=THT]
  R2 = Resistor [tolerance=±5% resistance=10k package=THT]
  R3 = Resistor [tolerance=±5% resistance=4.7k package=THT]
  U2 = Arduino Uno (Rev3)
  C1 = Electrolytic Capacitor [capacitance=33µF package="100 mil [THT, electrolytic]"]
  C2 = Electrolytic Capacitor [capacitance=1µF package="100 mil [THT, electrolytic]"]
  C3 = Ceramic Capacitor [capacitance=100nF package="100 mil [THT, multilayer]"]
  J1 = Screw terminal - 2 pins [package=THT]
  J2 = screw terminal, 3 pins

nets:
  N1: U1.connector0, U1.connector4, R2.Pin_1, C3.1
  N2: U1.connector1, R1.Pin_1, R2.Pin_0
  N3: U1.connector2, R3.Pin_1, C1.+
  GND: U1.connector3, R1.Pin_0, U2.GND, C1.-, C2.-, C3.0, J1.pin2, J2.pin3
  N4: U1.connector5, U1.connector6, C2.+, J1.pin1
  12V: U1.connector7, J2.pin1
  N5: R3.Pin_0, U2.D3_PWM
  5V: U2.5V, J2.pin2

notes:
  0-10V
