# Fritzing sketch PWM_to_0_10V_output (saved by Fritzing 0.9.0b)
breadboards: 1

parts:
  U2 = LM 358 Dual Op-Amp [package="DIP8 [THT]"]
  R1 = Resistor [tolerance=±5% resistance=10k package=THT]
  R2 = Resistor [tolerance=±5% resistance=10k package=THT]
  R3 = Resistor [tolerance=±5% resistance=4.7k package=THT]
  U1 = Arduino Uno (Rev3)
  C1 = Electrolytic Capacitor [capacitance=33µF package="100 mil [THT, electrolytic]"]
  C2 = Electrolytic Capacitor [capacitance=1µF package="100 mil [THT, electrolytic]"]
  C3 = Ceramic Capacitor [capacitance=100nF package="100 mil [THT, multilayer]"]
  J2 = Screw terminal - 2 pins [package=THT]
  J1 = screw terminal, 3 pins
  R4 = Resistor [tolerance=±5% resistance=10k package=THT]
  R5 = Resistor [tolerance=±5% resistance=10k package=THT]
  R6 = Resistor [tolerance=±5% resistance=4.7k package=THT]
  C4 = Electrolytic Capacitor [capacitance=33µF package="100 mil [THT, electrolytic]"]
  C5 = Electrolytic Capacitor [capacitance=1µF package="100 mil [THT, electrolytic]"]
  C6 = Ceramic Capacitor [capacitance=100nF package="100 mil [THT, multilayer]"]
  J3 = Screw terminal - 2 pins [package=THT]
  U3 = LM 358 Dual Op-Amp [package="DIP8 [THT]"]

nets:
  N1: U2.connector0, U2.connector4, R2.Pin_1, C3.1
  N2: U2.connector1, R1.Pin_1, R2.Pin_0
  N3: U2.connector2, R3.Pin_1, C1.+
  GND: U2.connector3, R1.Pin_0, U1.GND, C1.-, C2.-, C3.0, J2.pin2, J1.pin3, R5.Pin_0, C4.-, C5.-, C6.0, J3.pin2, U3.connector3
  N4: U2.connector5, U2.connector6, C2.+, J2.pin1
  12V: U2.connector7, J1.pin1, U3.connector7
  N5: R3.Pin_0, U1.D5_PWM
  N6: U1.D6_PWM, R6.Pin_0
  5V: U1.5V, J1.pin2
  N7: R4.Pin_0, R5.Pin_1, U3.connector1
  N8: R4.Pin_1, C6.1, U3.connector0, U3.connector4
  N9: R6.Pin_1, C4.+, U3.connector2
  N10: C5.+, J3.pin1, U3.connector5, U3.connector6

notes:
  0-10V
